// Logisim project prototype.circ as structural Verilog: 4 circuits, main circuit main
module main (
);

  wire A_out, and_1_out, and_2_out, button_1_out, cdm_8_mark5_1_p1, cdm_8_mark5_1_p2, cdm_8_mark5_1_p4,
       cdm_8_mark5_1_p5, cdm_8_mark5_1_p7, cdm_8_mark5_1_p8, cdm_8_mark5_1_p9, cdm_8_mark5_1_p10,
       cdm_8_mark5_1_p11, clock, code, D_out, data, flush, IO, keyboard, not_1_out, priority_encoder_1_gs,
       read, S_out, video, W_out;
  wire [2:0] priority_encoder_1_out;
  wire [6:0] keyboard_1_data;
  wire [7:0] bit_extender_1_out, cdm_8_mark5_1_p14, cdm_8_mark5_1_p15, controlled_buffer_1_out, register_1_q,
       vaddr;
  wire [15:0] cdm_8_mark5_1_p13;
  wire [31:0] video_buffer_1_row0, video_buffer_1_row1, video_buffer_1_row2, video_buffer_1_row3,
       video_buffer_1_row4, video_buffer_1_row5, video_buffer_1_row6, video_buffer_1_row7,
       video_buffer_1_row8, video_buffer_1_row9, video_buffer_1_row10, video_buffer_1_row11,
       video_buffer_1_row12, video_buffer_1_row13, video_buffer_1_row14, video_buffer_1_row15,
       video_buffer_1_row16, video_buffer_1_row17, video_buffer_1_row18, video_buffer_1_row19,
       video_buffer_1_row20, video_buffer_1_row21, video_buffer_1_row22, video_buffer_1_row23,
       video_buffer_1_row24, video_buffer_1_row25, video_buffer_1_row26, video_buffer_1_row27,
       video_buffer_1_row28, video_buffer_1_row29, video_buffer_1_row30, video_buffer_1_row31;

  // Probe on cdm_8_mark5_1_p4
  // Probe on cdm_8_mark5_1_p5
  // Probe on cdm_8_mark5_1_p2
  // Probe on cdm_8_mark5_1_p1
  Button button_1 (.out(button_1_out));
  Clock clock_1 (.out(clock));
  // Probe on cdm_8_mark5_1_p9
  // Probe on cdm_8_mark5_1_p8
  // Probe on cdm_8_mark5_1_p7
  // CdM_8_mark5 cdm_8_mark5_1: pin names not known; wires that end beside it: cdm_8_mark5_1_p1, cdm_8_mark5_1_p2, clock, cdm_8_mark5_1_p4, cdm_8_mark5_1_p5, button_1_out, cdm_8_mark5_1_p7, cdm_8_mark5_1_p8, cdm_8_mark5_1_p9, cdm_8_mark5_1_p10, cdm_8_mark5_1_p11, read, cdm_8_mark5_1_p13, cdm_8_mark5_1_p14, cdm_8_mark5_1_p15
  Decoder #(.disabled(0)) decoder_1 (.out0(code), .out1(data), .sel(cdm_8_mark5_1_p10), .en(cdm_8_mark5_1_p11));
  assign controlled_buffer_1_out = not_1_out ? cdm_8_mark5_1_p14 : 8'bz;  // Controlled_Buffer controlled_buffer_1
  not not_1 (not_1_out, read);
  assign cdm_8_mark5_1_p15 = read ? controlled_buffer_1_out : 8'bz;  // Controlled_Buffer controlled_buffer_2
  // Probe on cdm_8_mark5_1_p13
  // Probe on controlled_buffer_1_out
  and and_1 (and_1_out, data, ~IO);  // AND_Gate
  video_buffer video_buffer_1 (
    .vaddr(vaddr), .read(read), .video(video), .clock(clock), .data(controlled_buffer_1_out),
    .row0(video_buffer_1_row0), .row16(video_buffer_1_row16), .row1(video_buffer_1_row1),
    .row17(video_buffer_1_row17), .row2(video_buffer_1_row2), .row18(video_buffer_1_row18),
    .row3(video_buffer_1_row3), .row19(video_buffer_1_row19), .row4(video_buffer_1_row4),
    .row20(video_buffer_1_row20), .row5(video_buffer_1_row5), .row21(video_buffer_1_row21),
    .row6(video_buffer_1_row6), .row22(video_buffer_1_row22), .row7(video_buffer_1_row7),
    .row23(video_buffer_1_row23), .row8(video_buffer_1_row8), .row24(video_buffer_1_row24),
    .row9(video_buffer_1_row9), .row25(video_buffer_1_row25), .row10(video_buffer_1_row10),
    .row26(video_buffer_1_row26), .row11(video_buffer_1_row11), .row27(video_buffer_1_row27),
    .row12(video_buffer_1_row12), .row28(video_buffer_1_row28), .row13(video_buffer_1_row13),
    .row29(video_buffer_1_row29), .row14(video_buffer_1_row14), .row30(video_buffer_1_row30),
    .row15(video_buffer_1_row15), .row31(video_buffer_1_row31), .data_out(controlled_buffer_1_out),
    .flush(flush));
  // Probe on cdm_8_mark5_1_p13[7:0]
  // Probe on vaddr
  identify_video identify_video_1 (.addr(cdm_8_mark5_1_p13[7:0]), .data(data), .out_4(video), .vaddr(vaddr));
  indentify_flush indentify_flush_1 (.data(data), .addr(cdm_8_mark5_1_p13[7:0]), .read(read), .flush(flush));
  DotMatrix #(.inputtype("row"), .matrixcols(32), .matrixrows(32)) dotmatrix_1 (
    .row0(video_buffer_1_row0), .row1(video_buffer_1_row1), .row2(video_buffer_1_row2),
    .row3(video_buffer_1_row3), .row4(video_buffer_1_row4), .row5(video_buffer_1_row5),
    .row6(video_buffer_1_row6), .row7(video_buffer_1_row7), .row8(video_buffer_1_row8),
    .row9(video_buffer_1_row9), .row10(video_buffer_1_row10), .row11(video_buffer_1_row11),
    .row12(video_buffer_1_row12), .row13(video_buffer_1_row13), .row14(video_buffer_1_row14),
    .row15(video_buffer_1_row15), .row16(video_buffer_1_row16), .row17(video_buffer_1_row17),
    .row18(video_buffer_1_row18), .row19(video_buffer_1_row19), .row20(video_buffer_1_row20),
    .row21(video_buffer_1_row21), .row22(video_buffer_1_row22), .row23(video_buffer_1_row23),
    .row24(video_buffer_1_row24), .row25(video_buffer_1_row25), .row26(video_buffer_1_row26),
    .row27(video_buffer_1_row27), .row28(video_buffer_1_row28), .row29(video_buffer_1_row29),
    .row30(video_buffer_1_row30), .row31(video_buffer_1_row31));
  ROM #(.addrWidth(16)) rom_1 (.addr(cdm_8_mark5_1_p13), .data(controlled_buffer_1_out), .sel(code));
  // Probe on controlled_buffer_1_out
  RAM #(.addrWidth(16)) ram_1 (
    .addr(cdm_8_mark5_1_p13), .data(controlled_buffer_1_out), .sel(and_1_out), .clk(clock), .ld(read));  // open: clr
  assign controlled_buffer_1_out = and_2_out ? register_1_q : 8'bz;  // Controlled_Buffer controlled_buffer_3
  and and_2 (and_2_out, keyboard, read);
  and and_3 (keyboard, ~cdm_8_mark5_1_p13[0], cdm_8_mark5_1_p13[1], cdm_8_mark5_1_p13[2], cdm_8_mark5_1_p13[3], cdm_8_mark5_1_p13[4], ~cdm_8_mark5_1_p13[5], cdm_8_mark5_1_p13[6], ~cdm_8_mark5_1_p13[7]);  // AND_Gate
  Keyboard keyboard_1 (.clk(clock), .data(keyboard_1_data));  // open: re, clr, avail
  or or_1 (IO, keyboard, video);
  // Probe on keyboard_1_data
  and A (A_out, keyboard_1_data[0], ~keyboard_1_data[1], ~keyboard_1_data[2], ~keyboard_1_data[3], ~keyboard_1_data[4], keyboard_1_data[5], keyboard_1_data[6]);  // AND_Gate
  and D (D_out, ~keyboard_1_data[0], ~keyboard_1_data[1], keyboard_1_data[2], ~keyboard_1_data[3], ~keyboard_1_data[4], keyboard_1_data[5], keyboard_1_data[6]);  // AND_Gate
  and W (W_out, keyboard_1_data[0], keyboard_1_data[1], keyboard_1_data[2], ~keyboard_1_data[3], keyboard_1_data[4], keyboard_1_data[5], keyboard_1_data[6]);  // AND_Gate
  and S (S_out, keyboard_1_data[0], keyboard_1_data[1], ~keyboard_1_data[2], ~keyboard_1_data[3], keyboard_1_data[4], keyboard_1_data[5], keyboard_1_data[6]);  // AND_Gate
  // Probe on priority_encoder_1_out
  Priority_Encoder priority_encoder_1 (
    .in2(D_out), .in3(A_out), .in4(S_out), .in5(W_out), .out(priority_encoder_1_out),
    .gs(priority_encoder_1_gs));  // open: in0, in1, in6, in7, en_in, en_out
  // Probe on bit_extender_1_out
  assign bit_extender_1_out = {{5{1'b0}}, priority_encoder_1_out};  // Bit_Extender bit_extender_1
  Register register_1 (.D(bit_extender_1_out), .en(priority_encoder_1_gs), .Q(register_1_q), .clk(clock));  // open: clr

  // Notes on the sheet:
  //   contents of rom_1 (hex, n*v repeats v):
  //   d2 5e a e0 46 ba a e1 a d0 0 b0 d1 1 b5 dd 2d 0 d3 1 92 e3 2 87 92 e3 b d1 0 b4 1c a4 d1 1 b5 ee 9
  //   d0 1 b1 1d a1 d0 0 b0 d2 7 42 98 98 98 d3 60 1c d3 80 a e0 5 93 8a ee fa 95 95 14 b1 a3 d2 5f ab a1
  //   ee b7 d4
endmodule

module video_buffer (
  input  [7:0] vaddr,
  input  read,
  input  video,
  input  clock,
  input  [7:0] data,
  input  flush,
  output [31:0] row0,
  output [31:0] row16,
  output [31:0] row1,
  output [31:0] row17,
  output [7:0] data_out,
  output [31:0] row2,
  output [31:0] row18,
  output [31:0] row3,
  output [31:0] row19,
  output [31:0] row4,
  output [31:0] row20,
  output [31:0] row5,
  output [31:0] row21,
  output [31:0] row6,
  output [31:0] row22,
  output [31:0] row7,
  output [31:0] row23,
  output [31:0] row8,
  output [31:0] row24,
  output [31:0] row9,
  output [31:0] row25,
  output [31:0] row10,
  output [31:0] row26,
  output [31:0] row11,
  output [31:0] row27,
  output [31:0] row12,
  output [31:0] row28,
  output [31:0] row13,
  output [31:0] row29,
  output [31:0] row14,
  output [31:0] row30,
  output [31:0] row15,
  output [31:0] row31
);

  wire and_1_out, and_2_out, decoder_1_out0, decoder_1_out1, decoder_1_out2, decoder_1_out3, decoder_2_out0,
       decoder_2_out1, decoder_2_out2, decoder_2_out3, decoder_2_out4, decoder_2_out5, decoder_2_out6,
       decoder_2_out7, decoder_2_out8, decoder_2_out9, decoder_2_out10, decoder_2_out11, decoder_2_out12,
       decoder_2_out13, decoder_2_out14, decoder_2_out15, decoder_2_out16, decoder_2_out17, decoder_2_out18,
       decoder_2_out19, decoder_2_out20, decoder_2_out21, decoder_2_out22, decoder_2_out23, decoder_2_out24,
       decoder_2_out25, decoder_2_out26, decoder_2_out27, decoder_2_out28, decoder_2_out29, decoder_2_out30,
       decoder_2_out31, not_1_out, not_2_out;
  wire [7:0] multiplexer_1_out, multiplexer_2_out, multiplexer_3_out, multiplexer_4_out, multiplexer_5_out,
       multiplexer_6_out, multiplexer_6_out_2, multiplexer_6_out_3, multiplexer_6_out_4;
  wire [31:0] demultiplexer_1_out0, demultiplexer_1_out1, multiplexer_7_out, multiplexer_8_out, row0_t,
       row1_t, row2_t, row3_t, row4_t, row5_t, row6_t, row7_t, row8_t, row9_t, row10_t, row11_t, row12_t,
       row13_t, row14_t, row15_t, row16_t, row17_t, row18_t, row19_t, row20_t, row21_t, row22_t, row23_t,
       row24_t, row25_t, row26_t, row27_t, row28_t, row29_t, row30_t, row31_t, wrow0, wrow1, wrow2, wrow3,
       wrow4, wrow5, wrow6, wrow7, wrow8, wrow9, wrow10, wrow11, wrow12, wrow13, wrow14, wrow15, wrow16,
       wrow17, wrow18, wrow19, wrow20, wrow21, wrow22, wrow23, wrow24, wrow25, wrow26, wrow27, wrow28,
       wrow29, wrow30, wrow31;

  assign data_out = and_1_out ? multiplexer_1_out : 8'bz;  // Controlled_Buffer controlled_buffer_1
  and and_1 (and_1_out, video, read);
  not not_1 (not_1_out, read);
  Multiplexer #(.select(2), .width(8), .enable("false")) multiplexer_1 (
    .in0(multiplexer_6_out_4), .in1(multiplexer_6_out_3), .in2(multiplexer_6_out_2), .in3(multiplexer_6_out),
    .out(multiplexer_1_out), .sel(vaddr[1:0]));
  Decoder #(.select(2), .disabled(0)) decoder_1 (
    .out0(decoder_1_out0), .out1(decoder_1_out1), .out2(decoder_1_out2), .out3(decoder_1_out3),
    .sel(vaddr[1:0]), .en(not_1_out));
  Multiplexer #(.width(8), .enable("false")) multiplexer_2 (
    .in0(multiplexer_6_out_4), .in1(data), .out(multiplexer_2_out), .sel(decoder_1_out0));
  Multiplexer #(.width(8), .enable("false")) multiplexer_3 (
    .in0(multiplexer_6_out_3), .in1(data), .out(multiplexer_3_out), .sel(decoder_1_out1));
  Multiplexer #(.width(8), .enable("false")) multiplexer_4 (
    .in0(multiplexer_6_out_2), .in1(data), .out(multiplexer_4_out), .sel(decoder_1_out2));
  Multiplexer #(.width(8), .enable("false")) multiplexer_5 (
    .in0(multiplexer_6_out), .in1(data), .out(multiplexer_5_out), .sel(decoder_1_out3));
  Demultiplexer #(.width(32)) demultiplexer_1 (
    .out0(demultiplexer_1_out0), .out1(demultiplexer_1_out1),
    .in({multiplexer_2_out, multiplexer_3_out, multiplexer_4_out, multiplexer_5_out}), .sel(vaddr[6]),
    .en(not_1_out));
  Multiplexer #(.width(32), .enable("false")) multiplexer_6 (
    .in0(multiplexer_7_out), .in1(multiplexer_8_out),
    .out({multiplexer_6_out_4, multiplexer_6_out_3, multiplexer_6_out_2, multiplexer_6_out}), .sel(vaddr[6]));
  Multiplexer #(.select(4), .width(32), .enable("false")) multiplexer_7 (
    .in0(row0_t), .in1(row1_t), .in2(row2_t), .in3(row3_t), .in4(row4_t), .in5(row5_t), .in6(row6_t),
    .in7(row7_t), .in8(row8_t), .in9(row9_t), .in10(row10_t), .in11(row11_t), .in12(row12_t), .in13(row13_t),
    .in14(row14_t), .in15(row15_t), .out(multiplexer_7_out), .sel(vaddr[5:2]));
  Multiplexer #(.select(4), .width(32), .enable("false")) multiplexer_8 (
    .in0(row16_t), .in1(row17_t), .in2(row18_t), .in3(row19_t), .in4(row20_t), .in5(row21_t), .in6(row22_t),
    .in7(row23_t), .in8(row24_t), .in9(row25_t), .in10(row26_t), .in11(row27_t), .in12(row28_t),
    .in13(row29_t), .in14(row30_t), .in15(row31_t), .out(multiplexer_8_out), .sel(vaddr[5:2]));
  Demultiplexer #(.select(4), .width(32)) demultiplexer_2 (
    .out0(wrow0), .out1(wrow1), .out2(wrow2), .out3(wrow3), .out4(wrow4), .out5(wrow5), .out6(wrow6),
    .out7(wrow7), .out8(wrow8), .out9(wrow9), .out10(wrow10), .out11(wrow11), .out12(wrow12), .out13(wrow13),
    .out14(wrow14), .out15(wrow15), .in(demultiplexer_1_out0), .sel(vaddr[5:2]), .en(not_1_out));
  Demultiplexer #(.select(4), .width(32)) demultiplexer_3 (
    .out0(wrow16), .out1(wrow17), .out2(wrow18), .out3(wrow19), .out4(wrow20), .out5(wrow21), .out6(wrow22),
    .out7(wrow23), .out8(wrow24), .out9(wrow25), .out10(wrow26), .out11(wrow27), .out12(wrow28),
    .out13(wrow29), .out14(wrow30), .out15(wrow31), .in(demultiplexer_1_out1), .sel(vaddr[5:2]),
    .en(not_1_out));
  not not_2 (not_2_out, read);
  and and_2 (and_2_out, video, not_2_out);
  Decoder #(.select(5), .disabled(0)) decoder_2 (
    .out0(decoder_2_out0), .out1(decoder_2_out1), .out2(decoder_2_out2), .out3(decoder_2_out3),
    .out4(decoder_2_out4), .out5(decoder_2_out5), .out6(decoder_2_out6), .out7(decoder_2_out7),
    .out8(decoder_2_out8), .out9(decoder_2_out9), .out10(decoder_2_out10), .out11(decoder_2_out11),
    .out12(decoder_2_out12), .out13(decoder_2_out13), .out14(decoder_2_out14), .out15(decoder_2_out15),
    .out16(decoder_2_out16), .out17(decoder_2_out17), .out18(decoder_2_out18), .out19(decoder_2_out19),
    .out20(decoder_2_out20), .out21(decoder_2_out21), .out22(decoder_2_out22), .out23(decoder_2_out23),
    .out24(decoder_2_out24), .out25(decoder_2_out25), .out26(decoder_2_out26), .out27(decoder_2_out27),
    .out28(decoder_2_out28), .out29(decoder_2_out29), .out30(decoder_2_out30), .out31(decoder_2_out31),
    .sel(vaddr[6:2]), .en(and_2_out));
  Register #(.width(32)) register_1 (.D(wrow0), .en(decoder_2_out0), .Q(row0_t), .clk(clock));  // open: clr
  Register #(.width(32)) register_2 (.D(wrow1), .en(decoder_2_out1), .Q(row1_t), .clk(clock));  // open: clr
  Register #(.width(32)) register_3 (.D(wrow2), .en(decoder_2_out2), .Q(row2_t), .clk(clock));  // open: clr
  Register #(.width(32)) register_4 (.D(wrow3), .en(decoder_2_out3), .Q(row3_t), .clk(clock));  // open: clr
  Register #(.width(32)) register_5 (.D(wrow4), .en(decoder_2_out4), .Q(row4_t), .clk(clock));  // open: clr
  Register #(.width(32)) register_6 (.D(wrow5), .en(decoder_2_out5), .Q(row5_t), .clk(clock));  // open: clr
  Register #(.width(32)) register_7 (.D(wrow6), .en(decoder_2_out6), .Q(row6_t), .clk(clock));  // open: clr
  Register #(.width(32)) register_8 (.D(wrow7), .en(decoder_2_out7), .Q(row7_t), .clk(clock));  // open: clr
  Register #(.width(32)) register_9 (.D(wrow8), .en(decoder_2_out8), .Q(row8_t), .clk(clock));  // open: clr
  Register #(.width(32)) register_10 (.D(wrow9), .en(decoder_2_out9), .Q(row9_t), .clk(clock));  // open: clr
  Register #(.width(32)) register_11 (.D(wrow10), .en(decoder_2_out10), .Q(row10_t), .clk(clock));  // open: clr
  Register #(.width(32)) register_12 (.D(wrow11), .en(decoder_2_out11), .Q(row11_t), .clk(clock));  // open: clr
  Register #(.width(32)) register_13 (.D(wrow12), .en(decoder_2_out12), .Q(row12_t), .clk(clock));  // open: clr
  Register #(.width(32)) register_14 (.D(wrow13), .en(decoder_2_out13), .Q(row13_t), .clk(clock));  // open: clr
  Register #(.width(32)) register_15 (.D(wrow14), .en(decoder_2_out14), .Q(row14_t), .clk(clock));  // open: clr
  Register #(.width(32)) register_16 (.D(wrow15), .en(decoder_2_out15), .Q(row15_t), .clk(clock));  // open: clr
  Register #(.width(32)) register_17 (.D(wrow16), .en(decoder_2_out16), .Q(row16_t), .clk(clock));  // open: clr
  Register #(.width(32)) register_18 (.D(wrow17), .en(decoder_2_out17), .Q(row17_t), .clk(clock));  // open: clr
  Register #(.width(32)) register_19 (.D(wrow18), .en(decoder_2_out18), .Q(row18_t), .clk(clock));  // open: clr
  Register #(.width(32)) register_20 (.D(wrow19), .en(decoder_2_out19), .Q(row19_t), .clk(clock));  // open: clr
  Register #(.width(32)) register_21 (.D(wrow20), .en(decoder_2_out20), .Q(row20_t), .clk(clock));  // open: clr
  Register #(.width(32)) register_22 (.D(wrow21), .en(decoder_2_out21), .Q(row21_t), .clk(clock));  // open: clr
  Register #(.width(32)) register_23 (.D(wrow22), .en(decoder_2_out22), .Q(row22_t), .clk(clock));  // open: clr
  Register #(.width(32)) register_24 (.D(wrow23), .en(decoder_2_out23), .Q(row23_t), .clk(clock));  // open: clr
  Register #(.width(32)) register_25 (.D(wrow24), .en(decoder_2_out24), .Q(row24_t), .clk(clock));  // open: clr
  Register #(.width(32)) register_26 (.D(wrow25), .en(decoder_2_out25), .Q(row25_t), .clk(clock));  // open: clr
  Register #(.width(32)) register_27 (.D(wrow26), .en(decoder_2_out26), .Q(row26_t), .clk(clock));  // open: clr
  Register #(.width(32)) register_28 (.D(wrow27), .en(decoder_2_out27), .Q(row27_t), .clk(clock));  // open: clr
  Register #(.width(32)) register_29 (.D(wrow28), .en(decoder_2_out28), .Q(row28_t), .clk(clock));  // open: clr
  Register #(.width(32)) register_30 (.D(wrow29), .en(decoder_2_out29), .Q(row29_t), .clk(clock));  // open: clr
  Register #(.width(32)) register_31 (.D(wrow30), .en(decoder_2_out30), .Q(row30_t), .clk(clock));  // open: clr
  Register #(.width(32)) register_32 (.D(wrow31), .en(decoder_2_out31), .Q(row31_t), .clk(clock));  // open: clr
  Register #(.width(32)) register_33 (.D(row0_t), .Q(row0), .clk(flush));  // open: en, clr
  Register #(.width(32)) register_34 (.D(row1_t), .Q(row1), .clk(flush));  // open: en, clr
  Register #(.width(32)) register_35 (.D(row2_t), .Q(row2), .clk(flush));  // open: en, clr
  Register #(.width(32)) register_36 (.D(row3_t), .Q(row3), .clk(flush));  // open: en, clr
  Register #(.width(32)) register_37 (.D(row4_t), .Q(row4), .clk(flush));  // open: en, clr
  Register #(.width(32)) register_38 (.D(row5_t), .Q(row5), .clk(flush));  // open: en, clr
  Register #(.width(32)) register_39 (.D(row6_t), .Q(row6), .clk(flush));  // open: en, clr
  Register #(.width(32)) register_40 (.D(row7_t), .Q(row7), .clk(flush));  // open: en, clr
  Register #(.width(32)) register_41 (.D(row8_t), .Q(row8), .clk(flush));  // open: en, clr
  Register #(.width(32)) register_42 (.D(row9_t), .Q(row9), .clk(flush));  // open: en, clr
  Register #(.width(32)) register_43 (.D(row10_t), .Q(row10), .clk(flush));  // open: en, clr
  Register #(.width(32)) register_44 (.D(row11_t), .Q(row11), .clk(flush));  // open: en, clr
  Register #(.width(32)) register_45 (.D(row12_t), .Q(row12), .clk(flush));  // open: en, clr
  Register #(.width(32)) register_46 (.D(row13_t), .Q(row13), .clk(flush));  // open: en, clr
  Register #(.width(32)) register_47 (.D(row14_t), .Q(row14), .clk(flush));  // open: en, clr
  Register #(.width(32)) register_48 (.D(row15_t), .Q(row15), .clk(flush));  // open: en, clr
  Register #(.width(32)) register_49 (.D(row16_t), .Q(row16), .clk(flush));  // open: en, clr
  Register #(.width(32)) register_50 (.D(row17_t), .Q(row17), .clk(flush));  // open: en, clr
  Register #(.width(32)) register_51 (.D(row18_t), .Q(row18), .clk(flush));  // open: en, clr
  Register #(.width(32)) register_52 (.D(row19_t), .Q(row19), .clk(flush));  // open: en, clr
  Register #(.width(32)) register_53 (.D(row20_t), .Q(row20), .clk(flush));  // open: en, clr
  Register #(.width(32)) register_54 (.D(row21_t), .Q(row21), .clk(flush));  // open: en, clr
  Register #(.width(32)) register_55 (.D(row22_t), .Q(row22), .clk(flush));  // open: en, clr
  Register #(.width(32)) register_56 (.D(row23_t), .Q(row23), .clk(flush));  // open: en, clr
  Register #(.width(32)) register_57 (.D(row24_t), .Q(row24), .clk(flush));  // open: en, clr
  Register #(.width(32)) register_58 (.D(row25_t), .Q(row25), .clk(flush));  // open: en, clr
  Register #(.width(32)) register_59 (.D(row26_t), .Q(row26), .clk(flush));  // open: en, clr
  Register #(.width(32)) register_60 (.D(row27_t), .Q(row27), .clk(flush));  // open: en, clr
  Register #(.width(32)) register_61 (.D(row28_t), .Q(row28), .clk(flush));  // open: en, clr
  Register #(.width(32)) register_62 (.D(row29_t), .Q(row29), .clk(flush));  // open: en, clr
  Register #(.width(32)) register_63 (.D(row30_t), .Q(row30), .clk(flush));  // open: en, clr
  Register #(.width(32)) register_64 (.D(row31_t), .Q(row31), .clk(flush));  // open: en, clr

  // Notes on the sheet:
  //   Data
endmodule

module indentify_flush (
  input  data,
  input  [7:0] addr,
  input  read,
  output flush
);

  wire and_1_out;

  and and_1 (and_1_out, addr[0], addr[1], addr[2], addr[3], addr[4], ~addr[5], addr[6], ~addr[7]);  // AND_Gate
  and and_2 (flush, data, and_1_out, ~read);  // AND_Gate
endmodule

module identify_video (
  input  [7:0] addr,
  input  data,
  output [7:0] vaddr,
  output out_4
);

  wire [7:7] adder_1_out;

  // Probe on addr
  // Probe on {adder_1_out[7], vaddr[6:0]}
  Adder adder_1 (.a(addr), .b(8'h20), .out({adder_1_out[7], vaddr[6:0]}));  // open: cin, cout
  // Probe on {1'b0, vaddr[6:0]}
  and and_1 (out_4, adder_1_out[7], data);

  assign vaddr[7] = 1'b0;
endmodule
